// Logisim project CPU.circ as structural Verilog
module main (
  input  reset
);

  wire beq, beq_out, blt, blt_or_beq_mux_input_1_out_5, blt_out, clk, DWE, Immed_type, \input , j, jal,
       keyboard_1_avail, lw, memory_latch_1_oe_latched, memory_latch_1_we_latched, not_1_out, only_output,
       \output , PWE, RWE;
  wire [2:0] ALUOp, multiplexer_4_out, multiplexer_5_out, Rd, Rs1, Rs2, Shamt;
  wire [7:0] input_value;
  wire [11:0] address;
  wire [15:0] alu_circ_1_data_out, alu_circ_3_data_out, Immed, instruction, jal_address,
       memory_latch_1_address_latched, memory_latch_1_data_in_latched, multiplexer_1_out, multiplexer_2_out,
       multiplexer_3_out, multiplexer_6_out, multiplexer_7_out, multiplexer_8_out, multiplexer_9_out,
       ram_1_dout, reg16bit_1_data_out, registerfile_1_rs2_contents, rs;

  Multiplexer #(.width(16), .enable("false")) multiplexer_1 (
    .in0(multiplexer_2_out), .in1({multiplexer_2_out[15:12], address}), .out(multiplexer_1_out), .sel(jal));
  blt_or_beq_mux_input blt_or_beq_mux_input_1 (
    .blt(blt), .blt_out(blt_out), .beq(beq), .beq_out(beq_out), .out_5(blt_or_beq_mux_input_1_out_5));
  Multiplexer #(.width(16), .enable("false")) multiplexer_2 (
    .in0(jal_address), .in1(alu_circ_1_data_out), .out(multiplexer_2_out), .sel(blt_or_beq_mux_input_1_out_5));
  ALU_CIRC alu_circ_1 (.A(jal_address), .B(Immed), .shamt(3'b000), .optype(3'b001), .data_out(alu_circ_1_data_out));
  instruction_split instruction_split_1 (
    .address(address), .immed(Immed), .lw(lw), .beq(beq), .blt(blt), .j(j), .jal(jal), .\output (\output ),
    .\input (\input ), .ALUOp(ALUOp), .only_output(only_output), .Immed_type(Immed_type), .RWE(RWE),
    .DWE(DWE), .PWE(PWE), .data_in(instruction), .Shamt(Shamt), .Rd(Rd), .Rs(Rs1), .Rt(Rs2));
  ALU_CIRC alu_circ_2 (.A(multiplexer_3_out), .B(16'h1), .shamt(3'b000), .optype(3'b001), .data_out(jal_address));
  reg16bit reg16bit_1 (
    .in_1(multiplexer_1_out), .clk(clk), .write_enable(PWE), .reset(reset), .data_out(reg16bit_1_data_out));
  ROM #(.addrWidth(16), .dataWidth(16)) rom_1 (.addr(reg16bit_1_data_out), .data(instruction));
  Multiplexer #(.width(16), .enable("false")) multiplexer_3 (
    .in0(reg16bit_1_data_out), .in1({reg16bit_1_data_out[15:12], address}), .out(multiplexer_3_out), .sel(j));
  Multiplexer #(.width(3), .enable("false")) multiplexer_4 (
    .in0(Rd), .in1(Rs2), .out(multiplexer_4_out), .sel(Immed_type));
  Clock clock_1 (.out(clk));
  Multiplexer #(.width(3), .enable("false")) multiplexer_5 (
    .in0(multiplexer_4_out), .in1(3'b111), .out(multiplexer_5_out), .sel(jal));
  Multiplexer #(.width(16), .enable("false")) multiplexer_6 (
    .in0(multiplexer_8_out), .in1(ram_1_dout), .out(multiplexer_6_out), .sel(lw));
  Multiplexer #(.width(16), .enable("false")) multiplexer_7 (
    .in0(multiplexer_6_out), .in1({{8{1'b0}}, input_value}), .out(multiplexer_7_out), .sel(\input ));
  RegisterFile registerfile_1 (
    .rd(multiplexer_5_out), .data_in(multiplexer_7_out), .clk(clk), .write_enable(RWE), .reset(reset),
    .rs1(Rs1), .rs2(Rs2), .rs1_contents(rs), .rs2_contents(registerfile_1_rs2_contents));
  less_than_check less_than_check_1 (.in_1(alu_circ_3_data_out), .out_2(blt_out));
  equality_check equality_check_1 (.in_1(alu_circ_3_data_out), .out_2(beq_out));
  Multiplexer #(.width(16), .enable("false")) multiplexer_8 (
    .in0(alu_circ_3_data_out), .in1(jal_address), .out(multiplexer_8_out), .sel(jal));
  Multiplexer #(.width(16), .enable("false")) multiplexer_9 (
    .in0(registerfile_1_rs2_contents), .in1(Immed), .out(multiplexer_9_out), .sel(Immed_type));
  not not_1 (not_1_out, clk);
  RAM #(.addrWidth(16), .dataWidth(16), .trigger("high"), .databus("bibus")) ram_1 (
    .addr(memory_latch_1_address_latched), .we(memory_latch_1_we_latched), .oe(memory_latch_1_oe_latched),
    .din(memory_latch_1_data_in_latched), .dout(ram_1_dout));
  memory_latch memory_latch_1 (
    .address(alu_circ_3_data_out), .WE(DWE), .clk(clk), .data_in(registerfile_1_rs2_contents),
    .address_latched(memory_latch_1_address_latched), .WE_latched(memory_latch_1_we_latched),
    .OE_latched(memory_latch_1_oe_latched), .data_in_latched(memory_latch_1_data_in_latched));
  TTY #(.rows(13), .cols(80), .trigger("falling")) tty_1 (.data(rs[6:0]), .clk(not_1_out), .we(\output ), .clr(reset));
  ALU_CIRC alu_circ_3 (.A(rs), .B(multiplexer_9_out), .shamt(Shamt), .optype(ALUOp), .data_out(alu_circ_3_data_out));
  Keyboard keyboard_1 (.clk(clk), .re(\input ), .clr(reset), .avail(keyboard_1_avail), .data(input_value[6:0]));
  not not_2 (input_value[7], keyboard_1_avail);

  // Notes on the sheet:
  //   Instruction Decoder
  //   contents of rom_1 (hex, n*v repeats v):
  //   7000 60c0 604f 6090 3281 203f d00a 2206 c010 7488 6272 c007 6441 203f 6441 203f 203f
  //   Instruction Memory
  //   Register File
  //   Data Memory
  //   TTY
  //   Keyboard
endmodule

// PC
module reg16bit (
  input  [15:0] in_1,
  input  clk,
  input  write_enable,
  input  reset,
  output [15:0] data_out
);

  wire and_1_out;

  and and_1 (and_1_out, clk, write_enable);
  D_Flip_Flop d_ff_1 (.D(in_1[0]), .clk(and_1_out), .Q(data_out[0]), .reset(reset));  // open: Qn, preset
  D_Flip_Flop d_ff_2 (.D(in_1[1]), .clk(and_1_out), .Q(data_out[1]), .reset(reset));  // open: Qn, preset
  D_Flip_Flop d_ff_3 (.D(in_1[2]), .clk(and_1_out), .Q(data_out[2]), .reset(reset));  // open: Qn, preset
  D_Flip_Flop d_ff_4 (.D(in_1[3]), .clk(and_1_out), .Q(data_out[3]), .reset(reset));  // open: Qn, preset
  D_Flip_Flop d_ff_5 (.D(in_1[4]), .clk(and_1_out), .Q(data_out[4]), .reset(reset));  // open: Qn, preset
  D_Flip_Flop d_ff_6 (.D(in_1[5]), .clk(and_1_out), .Q(data_out[5]), .reset(reset));  // open: Qn, preset
  D_Flip_Flop d_ff_7 (.D(in_1[6]), .clk(and_1_out), .Q(data_out[6]), .reset(reset));  // open: Qn, preset
  D_Flip_Flop d_ff_8 (.D(in_1[7]), .clk(and_1_out), .Q(data_out[7]), .reset(reset));  // open: Qn, preset
  D_Flip_Flop d_ff_9 (.D(in_1[8]), .clk(and_1_out), .Q(data_out[8]), .reset(reset));  // open: Qn, preset
  D_Flip_Flop d_ff_10 (.D(in_1[9]), .clk(and_1_out), .Q(data_out[9]), .reset(reset));  // open: Qn, preset
  D_Flip_Flop d_ff_11 (.D(in_1[10]), .clk(and_1_out), .Q(data_out[10]), .reset(reset));  // open: Qn, preset
  D_Flip_Flop d_ff_12 (.D(in_1[11]), .clk(and_1_out), .Q(data_out[11]), .reset(reset));  // open: Qn, preset
  D_Flip_Flop d_ff_13 (.D(in_1[12]), .clk(and_1_out), .Q(data_out[12]), .reset(reset));  // open: Qn, preset
  D_Flip_Flop d_ff_14 (.D(in_1[13]), .clk(and_1_out), .Q(data_out[13]), .reset(reset));  // open: Qn, preset
  D_Flip_Flop d_ff_15 (.D(in_1[14]), .clk(and_1_out), .Q(data_out[14]), .reset(reset));  // open: Qn, preset
  D_Flip_Flop d_ff_16 (.D(in_1[15]), .clk(and_1_out), .Q(data_out[15]), .reset(reset));  // open: Qn, preset
endmodule

module RegisterFile (
  input  [2:0] rd,
  input  [15:0] data_in,
  input  clk,
  input  write_enable,
  input  reset,
  input  [2:0] rs1,
  input  [2:0] rs2,
  output [15:0] rs1_contents,
  output [15:0] rs2_contents
);

  wire decoder_1_out1, decoder_1_out2, decoder_1_out3, decoder_1_out4, decoder_1_out5, decoder_1_out6,
       decoder_1_out7, decoder_2_out0, decoder_2_out1, decoder_2_out2, decoder_2_out3, decoder_2_out4,
       decoder_2_out5, decoder_2_out6, decoder_2_out7, decoder_3_out0, decoder_3_out1, decoder_3_out2,
       decoder_3_out3, decoder_3_out4, decoder_3_out5, decoder_3_out6, decoder_3_out7, not_1_out;
  wire [15:0] reg16bit_1_data_out, reg16bit_2_data_out, reg16bit_3_data_out, reg16bit_4_data_out,
       reg16bit_5_data_out, reg16bit_6_data_out, reg16bit_7_data_out;

  Decoder #(.select(3)) decoder_1 (
    .out1(decoder_1_out1), .out2(decoder_1_out2), .out3(decoder_1_out3), .out4(decoder_1_out4),
    .out5(decoder_1_out5), .out6(decoder_1_out6), .out7(decoder_1_out7), .sel(rd), .en(write_enable));  // open: out0
  not not_1 (not_1_out, clk);
  reg16bit reg16bit_1 (
    .in_1(data_in), .clk(not_1_out), .write_enable(decoder_1_out1), .reset(reset),
    .data_out(reg16bit_1_data_out));
  reg16bit reg16bit_2 (
    .in_1(data_in), .clk(not_1_out), .write_enable(decoder_1_out2), .reset(reset),
    .data_out(reg16bit_2_data_out));
  reg16bit reg16bit_3 (
    .in_1(data_in), .clk(not_1_out), .write_enable(decoder_1_out3), .reset(reset),
    .data_out(reg16bit_3_data_out));
  reg16bit reg16bit_4 (
    .in_1(data_in), .clk(not_1_out), .write_enable(decoder_1_out4), .reset(reset),
    .data_out(reg16bit_4_data_out));
  reg16bit reg16bit_5 (
    .in_1(data_in), .clk(not_1_out), .write_enable(decoder_1_out5), .reset(reset),
    .data_out(reg16bit_5_data_out));
  reg16bit reg16bit_6 (
    .in_1(data_in), .clk(not_1_out), .write_enable(decoder_1_out6), .reset(reset),
    .data_out(reg16bit_6_data_out));
  reg16bit reg16bit_7 (
    .in_1(data_in), .clk(not_1_out), .write_enable(decoder_1_out7), .reset(reset),
    .data_out(reg16bit_7_data_out));
  Decoder #(.select(3), .enable("false")) decoder_2 (
    .out0(decoder_2_out0), .out1(decoder_2_out1), .out2(decoder_2_out2), .out3(decoder_2_out3),
    .out4(decoder_2_out4), .out5(decoder_2_out5), .out6(decoder_2_out6), .out7(decoder_2_out7), .sel(rs1));
  assign rs1_contents = decoder_2_out0 ? {16{1'b0}} : 16'bz;  // Controlled_Buffer controlled_buffer_1
  assign rs1_contents = decoder_2_out1 ? reg16bit_1_data_out : 16'bz;  // Controlled_Buffer controlled_buffer_2
  assign rs1_contents = decoder_2_out2 ? reg16bit_2_data_out : 16'bz;  // Controlled_Buffer controlled_buffer_3
  assign rs1_contents = decoder_2_out3 ? reg16bit_3_data_out : 16'bz;  // Controlled_Buffer controlled_buffer_4
  assign rs1_contents = decoder_2_out4 ? reg16bit_4_data_out : 16'bz;  // Controlled_Buffer controlled_buffer_5
  assign rs1_contents = decoder_2_out5 ? reg16bit_5_data_out : 16'bz;  // Controlled_Buffer controlled_buffer_6
  assign rs1_contents = decoder_2_out6 ? reg16bit_6_data_out : 16'bz;  // Controlled_Buffer controlled_buffer_7
  assign rs1_contents = decoder_2_out7 ? reg16bit_7_data_out : 16'bz;  // Controlled_Buffer controlled_buffer_8
  // Probe on reg16bit_4_data_out
  // Probe on reg16bit_5_data_out
  // Probe on reg16bit_6_data_out
  // Probe on reg16bit_7_data_out
  // Probe on reg16bit_3_data_out
  // Probe on reg16bit_2_data_out
  // Probe on reg16bit_1_data_out
  // Probe on {16{1'b0}}
  Decoder #(.select(3), .enable("false")) decoder_3 (
    .out0(decoder_3_out0), .out1(decoder_3_out1), .out2(decoder_3_out2), .out3(decoder_3_out3),
    .out4(decoder_3_out4), .out5(decoder_3_out5), .out6(decoder_3_out6), .out7(decoder_3_out7), .sel(rs2));
  assign rs2_contents = decoder_3_out0 ? {16{1'b0}} : 16'bz;  // Controlled_Buffer controlled_buffer_9
  assign rs2_contents = decoder_3_out1 ? reg16bit_1_data_out : 16'bz;  // Controlled_Buffer controlled_buffer_10
  assign rs2_contents = decoder_3_out2 ? reg16bit_2_data_out : 16'bz;  // Controlled_Buffer controlled_buffer_11
  assign rs2_contents = decoder_3_out3 ? reg16bit_3_data_out : 16'bz;  // Controlled_Buffer controlled_buffer_12
  assign rs2_contents = decoder_3_out4 ? reg16bit_4_data_out : 16'bz;  // Controlled_Buffer controlled_buffer_13
  assign rs2_contents = decoder_3_out5 ? reg16bit_5_data_out : 16'bz;  // Controlled_Buffer controlled_buffer_14
  assign rs2_contents = decoder_3_out6 ? reg16bit_6_data_out : 16'bz;  // Controlled_Buffer controlled_buffer_15
  assign rs2_contents = decoder_3_out7 ? reg16bit_7_data_out : 16'bz;  // Controlled_Buffer controlled_buffer_16
endmodule

module sixteenbitadder (
  input  ABottom,
  input  in_2,
  input  in_3,
  input  in_4,
  input  in_5,
  input  in_6,
  input  in_7,
  input  in_8,
  input  in_9,
  input  in_10,
  input  in_11,
  input  in_12,
  input  in_13,
  input  in_14,
  input  in_15,
  input  ATop,
  input  BTop,
  input  in_18,
  input  in_19,
  input  in_20,
  input  in_21,
  input  in_22,
  input  in_23,
  input  in_24,
  input  in_25,
  input  in_26,
  input  in_27,
  input  in_28,
  input  in_29,
  input  in_30,
  input  in_31,
  input  BBottom,
  input  ESub,
  output OTop,
  output out_35,
  output out_36,
  output out_37,
  output out_38,
  output out_39,
  output out_40,
  output out_41,
  output out_42,
  output out_43,
  output out_44,
  output out_45,
  output out_46,
  output out_47,
  output out_48,
  output OTop_2,
  output Ccout
);

  wire onebitadder_1_carryout, onebitadder_2_carryout, onebitadder_3_carryout, onebitadder_4_carryout,
       onebitadder_5_carryout, onebitadder_6_carryout, onebitadder_7_carryout, onebitadder_8_carryout,
       onebitadder_9_carryout, onebitadder_10_carryout, onebitadder_11_carryout, onebitadder_12_carryout,
       onebitadder_13_carryout, onebitadder_14_carryout, onebitadder_15_carryout, onebitadder_16_carryout;

  onebitadder onebitadder_1 (
    .A(ATop), .B(BTop), .S(ESub), .CarryIn(ESub), .CarryOut(onebitadder_1_carryout), .Sum(OTop));
  onebitadder onebitadder_2 (
    .A(in_15), .B(in_18), .S(ESub), .CarryIn(onebitadder_1_carryout), .CarryOut(onebitadder_2_carryout),
    .Sum(out_35));
  onebitadder onebitadder_3 (
    .A(in_14), .B(in_19), .S(ESub), .CarryIn(onebitadder_2_carryout), .CarryOut(onebitadder_3_carryout),
    .Sum(out_36));
  onebitadder onebitadder_4 (
    .A(in_13), .B(in_20), .S(ESub), .CarryIn(onebitadder_3_carryout), .CarryOut(onebitadder_4_carryout),
    .Sum(out_37));
  onebitadder onebitadder_5 (
    .A(in_12), .B(in_21), .S(ESub), .CarryIn(onebitadder_4_carryout), .CarryOut(onebitadder_5_carryout),
    .Sum(out_38));
  onebitadder onebitadder_6 (
    .A(in_11), .B(in_22), .S(ESub), .CarryIn(onebitadder_5_carryout), .CarryOut(onebitadder_6_carryout),
    .Sum(out_39));
  onebitadder onebitadder_7 (
    .A(in_10), .B(in_23), .S(ESub), .CarryIn(onebitadder_6_carryout), .CarryOut(onebitadder_7_carryout),
    .Sum(out_40));
  onebitadder onebitadder_8 (
    .A(in_9), .B(in_24), .S(ESub), .CarryIn(onebitadder_7_carryout), .CarryOut(onebitadder_8_carryout),
    .Sum(out_41));
  onebitadder onebitadder_9 (
    .A(in_8), .B(in_25), .S(ESub), .CarryIn(onebitadder_8_carryout), .CarryOut(onebitadder_9_carryout),
    .Sum(out_42));
  onebitadder onebitadder_10 (
    .A(in_7), .B(in_26), .S(ESub), .CarryIn(onebitadder_9_carryout), .CarryOut(onebitadder_10_carryout),
    .Sum(out_43));
  onebitadder onebitadder_11 (
    .A(in_6), .B(in_27), .S(ESub), .CarryIn(onebitadder_10_carryout), .CarryOut(onebitadder_11_carryout),
    .Sum(out_44));
  onebitadder onebitadder_12 (
    .A(in_5), .B(in_28), .S(ESub), .CarryIn(onebitadder_11_carryout), .CarryOut(onebitadder_12_carryout),
    .Sum(out_45));
  onebitadder onebitadder_13 (
    .A(in_4), .B(in_29), .S(ESub), .CarryIn(onebitadder_12_carryout), .CarryOut(onebitadder_13_carryout),
    .Sum(out_46));
  onebitadder onebitadder_14 (
    .A(in_3), .B(in_30), .S(ESub), .CarryIn(onebitadder_13_carryout), .CarryOut(onebitadder_14_carryout),
    .Sum(out_47));
  onebitadder onebitadder_15 (
    .A(in_2), .B(in_31), .S(ESub), .CarryIn(onebitadder_14_carryout), .CarryOut(onebitadder_15_carryout),
    .Sum(out_48));
  onebitadder onebitadder_16 (
    .A(ABottom), .B(BBottom), .S(ESub), .CarryIn(onebitadder_15_carryout),
    .CarryOut(onebitadder_16_carryout), .Sum(OTop_2));
  xor xor_1 (Ccout, onebitadder_15_carryout, onebitadder_16_carryout);
endmodule

module onebitadder (
  input  CarryIn,
  input  A,
  input  B,
  input  S,
  output Sum,
  output CarryOut
);

  wire and_1_out, and_2_out, xor_1_out, xor_2_out;

  xor xor_1 (xor_1_out, B, S);
  and and_1 (and_1_out, A, xor_1_out);
  xor xor_2 (xor_2_out, A, xor_1_out);
  or or_1 (CarryOut, and_1_out, and_2_out);
  and and_2 (and_2_out, xor_2_out, CarryIn);
  xor xor_3 (Sum, CarryIn, xor_2_out);
endmodule

module ALU_CIRC (
  input  [15:0] A,
  input  [15:0] B,
  input  [2:0] shamt,
  input  [2:0] optype,
  output [15:0] data_out
);

  wire [15:0] and_1_out, left_shift_1_data_out, or_1_out, right_shift_1_data_out, sixteenbitadder_1_otop,
       sixteenbitadder_2_otop;

  assign and_1_out = A & B;  // AND_Gate and_1, 16 bits wide
  assign or_1_out = A | B;  // OR_Gate or_1, 16 bits wide
  right_shift right_shift_1 (.data_in(A), .shamt(shamt), .data_out(right_shift_1_data_out));
  left_shift left_shift_1 (.data_in(A), .shamt(shamt), .data_out(left_shift_1_data_out));
  sixteenbitadder sixteenbitadder_1 (
    .BTop(B[0]), .in_18(B[1]), .in_19(B[2]), .in_20(B[3]), .in_21(B[4]), .in_22(B[5]), .in_23(B[6]),
    .in_24(B[7]), .in_25(B[8]), .in_26(B[9]), .in_27(B[10]), .in_28(B[11]), .in_29(B[12]), .in_30(B[13]),
    .in_31(B[14]), .BBottom(B[15]), .ABottom(A[15]), .in_2(A[14]), .in_3(A[13]), .in_4(A[12]), .in_5(A[11]),
    .in_6(A[10]), .in_7(A[9]), .in_8(A[8]), .in_9(A[7]), .in_10(A[6]), .in_11(A[5]), .in_12(A[4]),
    .in_13(A[3]), .in_14(A[2]), .in_15(A[1]), .ATop(A[0]), .OTop(sixteenbitadder_1_otop[0]),
    .out_35(sixteenbitadder_1_otop[1]), .out_36(sixteenbitadder_1_otop[2]),
    .out_37(sixteenbitadder_1_otop[3]), .out_38(sixteenbitadder_1_otop[4]),
    .out_39(sixteenbitadder_1_otop[5]), .out_40(sixteenbitadder_1_otop[6]),
    .out_41(sixteenbitadder_1_otop[7]), .out_42(sixteenbitadder_1_otop[8]),
    .out_43(sixteenbitadder_1_otop[9]), .out_44(sixteenbitadder_1_otop[10]),
    .out_45(sixteenbitadder_1_otop[11]), .out_46(sixteenbitadder_1_otop[12]),
    .out_47(sixteenbitadder_1_otop[13]), .out_48(sixteenbitadder_1_otop[14]),
    .OTop_2(sixteenbitadder_1_otop[15]));  // open: ESub, Ccout
  sixteenbitadder sixteenbitadder_2 (
    .BTop(B[0]), .in_18(B[1]), .in_19(B[2]), .in_20(B[3]), .in_21(B[4]), .in_22(B[5]), .in_23(B[6]),
    .in_24(B[7]), .in_25(B[8]), .in_26(B[9]), .in_27(B[10]), .in_28(B[11]), .in_29(B[12]), .in_30(B[13]),
    .in_31(B[14]), .BBottom(B[15]), .ABottom(A[15]), .in_2(A[14]), .in_3(A[13]), .in_4(A[12]), .in_5(A[11]),
    .in_6(A[10]), .in_7(A[9]), .in_8(A[8]), .in_9(A[7]), .in_10(A[6]), .in_11(A[5]), .in_12(A[4]),
    .in_13(A[3]), .in_14(A[2]), .in_15(A[1]), .ATop(A[0]), .ESub(1'b1), .OTop(sixteenbitadder_2_otop[0]),
    .out_35(sixteenbitadder_2_otop[1]), .out_36(sixteenbitadder_2_otop[2]),
    .out_37(sixteenbitadder_2_otop[3]), .out_38(sixteenbitadder_2_otop[4]),
    .out_39(sixteenbitadder_2_otop[5]), .out_40(sixteenbitadder_2_otop[6]),
    .out_41(sixteenbitadder_2_otop[7]), .out_42(sixteenbitadder_2_otop[8]),
    .out_43(sixteenbitadder_2_otop[9]), .out_44(sixteenbitadder_2_otop[10]),
    .out_45(sixteenbitadder_2_otop[11]), .out_46(sixteenbitadder_2_otop[12]),
    .out_47(sixteenbitadder_2_otop[13]), .out_48(sixteenbitadder_2_otop[14]),
    .OTop_2(sixteenbitadder_2_otop[15]));  // open: Ccout
  Multiplexer #(.select(3), .width(16), .enable("false")) multiplexer_1 (
    .in0({16{1'b0}}), .in1(sixteenbitadder_1_otop), .in2(sixteenbitadder_2_otop), .in3(and_1_out),
    .in4(or_1_out), .in5({16{1'b0}}), .in6(right_shift_1_data_out), .in7(left_shift_1_data_out),
    .out(data_out), .sel(optype));
endmodule

module instruction_split (
  input  [15:0] data_in,
  output [11:0] address,
  output lw,
  output beq,
  output blt,
  output j,
  output jal,
  output \output ,
  output \input ,
  output [2:0] ALUOp,
  output only_output,
  output Immed_type,
  output RWE,
  output DWE,
  output PWE,
  output [15:0] immed,
  output [2:0] Shamt,
  output [2:0] Rd,
  output [2:0] Rs,
  output [2:0] Rt
);

  wire decoder_1_out4, decoder_1_out5, decoder_1_out6, decoder_1_out7, decoder_1_out8, decoder_1_out9,
       decoder_1_out10, decoder_1_out11;

  assign immed = {{10{data_in[5]}}, data_in[5:0]};  // Bit_Extender bit_extender_1
  Decoder #(.select(4)) decoder_1 (
    .out0(lw), .out1(DWE), .out2(beq), .out3(blt), .out4(decoder_1_out4), .out5(decoder_1_out5),
    .out6(decoder_1_out6), .out7(decoder_1_out7), .out8(decoder_1_out8), .out9(decoder_1_out9),
    .out10(decoder_1_out10), .out11(decoder_1_out11), .out12(j), .out13(jal), .out14(only_output),
    .out15(\input ), .sel(data_in[15:12]));  // open: en
  or or_1 (ALUOp[2], decoder_1_out11, only_output, decoder_1_out10, decoder_1_out4);
  or or_2 (ALUOp[1], decoder_1_out9, decoder_1_out8, decoder_1_out11, blt, decoder_1_out10, decoder_1_out5, beq);
  or or_3 (ALUOp[0], lw, decoder_1_out7, decoder_1_out11, only_output, decoder_1_out6, decoder_1_out5, DWE);
  or or_4 (Immed_type, lw, DWE, decoder_1_out6, decoder_1_out9);
  or or_5 (RWE, \input , jal, decoder_1_out11, decoder_1_out10, decoder_1_out9, decoder_1_out8, decoder_1_out7, decoder_1_out6, decoder_1_out5, decoder_1_out4, lw);

  assign address = data_in[11:0];
  assign \output  = only_output;
  assign PWE = 1'b1;
  assign Rd = data_in[5:3];
  assign Rs = data_in[11:9];
  assign Rt = data_in[8:6];
  assign Shamt = data_in[2:0];

  // Notes on the sheet:
  //   lw
  //   sw
  //   beq
  //   blt
  //   or
  //   and
  //   and
  //   addi
  //   add
  //   sub
  //   subi
  //   shr
  //   shl
  //   j
  //   jal
  //   output
  //   input
endmodule

module right_shift (
  input  [15:0] data_in,
  input  [2:0] shamt,
  output [15:0] data_out
);

  wire decoder_1_out0, decoder_1_out1, decoder_1_out2, decoder_1_out3, decoder_1_out4, decoder_1_out5,
       decoder_1_out6, decoder_1_out7;

  assign data_out = decoder_1_out0 ? data_in : 16'bz;  // Controlled_Buffer controlled_buffer_1
  Decoder #(.select(3)) decoder_1 (
    .out0(decoder_1_out0), .out1(decoder_1_out1), .out2(decoder_1_out2), .out3(decoder_1_out3),
    .out4(decoder_1_out4), .out5(decoder_1_out5), .out6(decoder_1_out6), .out7(decoder_1_out7), .sel(shamt));  // open: en
  assign data_out = decoder_1_out1 ? {1'b0, data_in[15:1]} : 16'bz;  // Controlled_Buffer controlled_buffer_2
  assign data_out = decoder_1_out2 ? {2'b00, data_in[15:2]} : 16'bz;  // Controlled_Buffer controlled_buffer_3
  assign data_out = decoder_1_out3 ? {3'b000, data_in[15:3]} : 16'bz;  // Controlled_Buffer controlled_buffer_4
  assign data_out = decoder_1_out4 ? {4'b0000, data_in[15:4]} : 16'bz;  // Controlled_Buffer controlled_buffer_5
  assign data_out = decoder_1_out5 ? {{5{1'b0}}, data_in[15:5]} : 16'bz;  // Controlled_Buffer controlled_buffer_6
  assign data_out = decoder_1_out6 ? {{6{1'b0}}, data_in[15:6]} : 16'bz;  // Controlled_Buffer controlled_buffer_7
  assign data_out = decoder_1_out7 ? {{7{1'b0}}, data_in[15:7]} : 16'bz;  // Controlled_Buffer controlled_buffer_8
endmodule

module left_shift (
  input  [15:0] data_in,
  input  [2:0] shamt,
  output [15:0] data_out
);

  wire decoder_1_out0, decoder_1_out1, decoder_1_out2, decoder_1_out3, decoder_1_out4, decoder_1_out5,
       decoder_1_out6, decoder_1_out7;

  assign data_out = decoder_1_out0 ? data_in : 16'bz;  // Controlled_Buffer controlled_buffer_1
  Decoder #(.select(3)) decoder_1 (
    .out0(decoder_1_out0), .out1(decoder_1_out1), .out2(decoder_1_out2), .out3(decoder_1_out3),
    .out4(decoder_1_out4), .out5(decoder_1_out5), .out6(decoder_1_out6), .out7(decoder_1_out7), .sel(shamt));  // open: en
  assign data_out = decoder_1_out1 ? {data_in[14:0], 1'b0} : 16'bz;  // Controlled_Buffer controlled_buffer_2
  assign data_out = decoder_1_out2 ? {data_in[13:0], 2'b00} : 16'bz;  // Controlled_Buffer controlled_buffer_3
  assign data_out = decoder_1_out3 ? {data_in[12:0], 3'b000} : 16'bz;  // Controlled_Buffer controlled_buffer_4
  assign data_out = decoder_1_out4 ? {data_in[11:0], 4'b0000} : 16'bz;  // Controlled_Buffer controlled_buffer_5
  assign data_out = decoder_1_out5 ? {data_in[10:0], {5{1'b0}}} : 16'bz;  // Controlled_Buffer controlled_buffer_6
  assign data_out = decoder_1_out6 ? {data_in[9:0], {6{1'b0}}} : 16'bz;  // Controlled_Buffer controlled_buffer_7
  assign data_out = decoder_1_out7 ? {data_in[8:0], {7{1'b0}}} : 16'bz;  // Controlled_Buffer controlled_buffer_8
endmodule

module memory_latch (
  input  [15:0] address,
  input  WE,
  input  clk,
  input  [15:0] data_in,
  output [15:0] address_latched,
  output WE_latched,
  output OE_latched,
  output [15:0] data_in_latched
);

  wire d_ff_1_q;
  wire [15:0] register_1_q;

  Register #(.width(16), .trigger("falling")) register_1 (
    .D(address), .en(WE), .clk(clk), .Q(register_1_q));  // open: clr
  D_Flip_Flop #(.trigger("falling")) d_ff_1 (.D(WE), .clk(clk), .Q(d_ff_1_q));  // open: Qn, preset, reset
  Register #(.width(16), .trigger("falling")) register_2 (
    .D(data_in), .en(WE), .clk(clk), .Q(data_in_latched));  // open: clr
  Multiplexer #(.width(16), .enable("false")) multiplexer_1 (
    .in0(address), .in1(register_1_q), .out(address_latched), .sel(d_ff_1_q));
  and and_1 (WE_latched, clk, d_ff_1_q);
  not not_1 (OE_latched, WE_latched);
endmodule

module equality_check (
  input  [15:0] in_1,
  output out_2
);

  wire [15:0] not_1_out;

  assign not_1_out = ~in_1;  // NOT_Gate not_1, 16 bits wide
  and and_1 (out_2, not_1_out[0], not_1_out[1], not_1_out[2], not_1_out[3], not_1_out[4], not_1_out[5], not_1_out[6], not_1_out[7], not_1_out[9], not_1_out[10], not_1_out[11], not_1_out[12], not_1_out[13], not_1_out[14], not_1_out[15], not_1_out[8]);
endmodule

module less_than_check (
  input  [15:0] in_1,
  output out_2
);


  assign out_2 = in_1[15];
endmodule

module blt_or_beq_mux_input (
  input  blt,
  input  blt_out,
  input  beq,
  input  beq_out,
  output out_5
);

  wire and_1_out, and_2_out;

  and and_1 (and_1_out, blt, blt_out);
  and and_2 (and_2_out, beq, beq_out);
  or or_1 (out_5, and_1_out, and_2_out);
endmodule
